// Logisim project 32位全加器全减器.circ as structural Verilog: 11 circuits, main circuit 8bit加法最终版
module \_8bit加法  (
  input  C0,
  input  A0,
  input  B0,
  input  A1,
  input  B1,
  input  A2,
  input  B2,
  input  A3,
  input  B3,
  input  A4,
  input  B4,
  input  A5,
  input  B5,
  input  A6,
  input  B6,
  input  A7,
  input  B7,
  output S0,
  output S1,
  output S2,
  output S3,
  output S4,
  output S5,
  output S6,
  output S7,
  output C7
);

  wire \n4bit加法_1_c4 ;

  \_4bit加法  \u_4bit加法_1  (
    .C4(\n4bit加法_1_c4 ), .S3(S3), .S0(S0), .S1(S1), .S2(S2), .A0(A0), .B0(B0), .C0(C0), .A1(A1), .B1(B1),
    .A2(A2), .B2(B2), .A3(A3), .B3(B3));
  \_4bit加法  \u_4bit加法_2  (
    .C4(C7), .S3(S7), .S0(S4), .S1(S5), .S2(S6), .A0(A4), .B0(B4), .C0(\n4bit加法_1_c4 ), .A1(A5), .B1(B5),
    .A2(A6), .B2(B6), .A3(A7), .B3(B7));
endmodule

module \_1bit加法  (
  input  A,
  input  B,
  input  Ci,
  output Co,
  output S
);

  wire and_1_out, and_2_out, and_3_out, and_4_out, and_5_out, and_6_out, and_7_out, and_8_out, and_9_out,
       and_10_out, and_11_out, not_1_out, not_2_out, not_3_out, not_4_out, not_5_out, not_6_out, or_1_out,
       or_3_out, or_4_out;

  and and_1 (and_1_out, B, Ci);
  and and_2 (and_2_out, A, Ci);
  not not_1 (not_1_out, B);
  not not_2 (not_2_out, A);
  not not_3 (not_3_out, A);
  not not_4 (not_4_out, B);
  or or_1 (or_1_out, and_1_out, and_2_out);
  and and_3 (and_3_out, A, B);
  and and_4 (and_4_out, A, not_1_out);
  not not_5 (not_5_out, Ci);
  and and_5 (and_5_out, not_2_out, B);
  not not_6 (not_6_out, Ci);
  and and_6 (and_6_out, not_3_out, not_4_out);
  and and_7 (and_7_out, A, B);
  or or_2 (Co, or_1_out, and_3_out);
  and and_8 (and_8_out, and_4_out, not_5_out);
  and and_9 (and_9_out, and_5_out, not_6_out);
  and and_10 (and_10_out, and_6_out, Ci);
  and and_11 (and_11_out, and_7_out, Ci);
  or or_3 (or_3_out, and_8_out, and_9_out);
  or or_4 (or_4_out, and_10_out, and_11_out);
  or or_5 (S, or_3_out, or_4_out);
endmodule

module \_4bit加法  (
  input  C0,
  input  A0,
  input  B0,
  input  A1,
  input  B1,
  input  A2,
  input  B2,
  input  A3,
  input  B3,
  output S0,
  output S1,
  output S2,
  output S3,
  output C4
);

  wire \n1bit加法_1_co , \n1bit加法_2_co , \n1bit加法_3_co ;

  \_1bit加法  \u_1bit加法_1  (.A(A0), .B(B0), .Ci(C0), .Co(\n1bit加法_1_co ), .S(S0));
  \_1bit加法  \u_1bit加法_2  (.A(A1), .B(B1), .Ci(\n1bit加法_1_co ), .Co(\n1bit加法_2_co ), .S(S1));
  \_1bit加法  \u_1bit加法_3  (.A(A2), .B(B2), .Ci(\n1bit加法_2_co ), .Co(\n1bit加法_3_co ), .S(S2));
  \_1bit加法  \u_1bit加法_4  (.A(A3), .B(B3), .Ci(\n1bit加法_3_co ), .Co(C4), .S(S3));
endmodule

module \_8bit加法最终版  (
  input  Cin,
  input  [7:0] B,
  input  [7:0] A,
  output [7:0] S,
  output Cout
);

  \_8bit加法  \u_8bit加法_1  (
    .C0(Cin), .C7(Cout), .S0(S[0]), .S1(S[1]), .S2(S[2]), .S3(S[3]), .S4(S[4]), .S5(S[5]), .S6(S[6]),
    .S7(S[7]), .A0(A[0]), .B0(B[0]), .A1(A[1]), .B1(B[1]), .A2(A[2]), .B2(B[2]), .A3(A[3]), .B3(B[3]),
    .A4(A[4]), .B4(B[4]), .A5(A[5]), .B5(B[5]), .A6(A[6]), .B6(B[6]), .A7(A[7]), .B7(B[7]));
endmodule

module \_32bit加法最终版  (
  input  Cin,
  input  [31:0] A,
  input  [31:0] A_2,
  output [31:0] S,
  output Cout
);

  wire \n8bit加法最终版_2_cout , \n8bit加法最终版_3_cout , \n8bit加法最终版_4_cout ;

  \_8bit加法最终版  \u_8bit加法最终版_1  (.Cout(Cout), .S(S[31:24]), .B(A[30:23]), .A(A_2[31:24]), .Cin(\n8bit加法最终版_2_cout ));
  \_8bit加法最终版  \u_8bit加法最终版_2  (
    .Cout(\n8bit加法最终版_2_cout ), .S(S[23:16]), .B(A[23:16]), .A(A_2[23:16]), .Cin(\n8bit加法最终版_3_cout ));
  \_8bit加法最终版  \u_8bit加法最终版_3  (
    .Cout(\n8bit加法最终版_3_cout ), .S(S[15:8]), .B(A[15:8]), .A(A_2[15:8]), .Cin(\n8bit加法最终版_4_cout ));
  \_8bit加法最终版  \u_8bit加法最终版_4  (.Cout(\n8bit加法最终版_4_cout ), .S(S[7:0]), .B(A[7:0]), .A(A_2[7:0]), .Cin(Cin));
endmodule

module \_1bit减法  (
  input  A,
  input  B,
  input  Ci1,
  output Ci,
  output S
);

  wire and_1_out, and_2_out, and_3_out, and_4_out, and_5_out, and_6_out, and_7_out, and_8_out, and_9_out,
       and_10_out, and_11_out, not_1_out, not_2_out, not_3_out, not_4_out, not_5_out, not_6_out, not_7_out,
       not_8_out, or_1_out, or_3_out, or_4_out;

  not not_1 (not_1_out, A);
  not not_2 (not_2_out, A);
  not not_3 (not_3_out, Ci1);
  not not_4 (not_4_out, A);
  not not_5 (not_5_out, Ci1);
  not not_6 (not_6_out, A);
  and and_1 (and_1_out, not_1_out, B);
  and and_2 (and_2_out, Ci1, not_2_out);
  and and_3 (and_3_out, not_3_out, not_4_out);
  and and_4 (and_4_out, not_5_out, A);
  not not_7 (not_7_out, B);
  and and_5 (and_5_out, Ci1, not_6_out);
  not not_8 (not_8_out, B);
  and and_6 (and_6_out, Ci1, A);
  or or_1 (or_1_out, and_1_out, and_2_out);
  and and_7 (and_7_out, Ci1, B);
  and and_8 (and_8_out, and_3_out, B);
  and and_9 (and_9_out, and_4_out, not_7_out);
  and and_10 (and_10_out, and_5_out, not_8_out);
  and and_11 (and_11_out, and_6_out, B);
  or or_2 (Ci, or_1_out, and_7_out);
  or or_3 (or_3_out, and_8_out, and_9_out);
  or or_4 (or_4_out, and_10_out, and_11_out);
  or or_5 (S, or_3_out, or_4_out);
endmodule

module \_8bit减法  (
  input  A0,
  input  B0,
  input  Ci_1,
  input  A1,
  input  B1,
  input  A2,
  input  B2,
  input  A3,
  input  B3,
  input  A4,
  input  B4,
  input  A5,
  input  B5,
  input  A6,
  input  B6,
  input  A7,
  input  B7,
  output [7:0] S,
  output Ci
);

  wire \n1bit减法_1_ci , \n1bit减法_2_ci , \n1bit减法_3_ci , \n1bit减法_4_ci , \n1bit减法_5_ci , \n1bit减法_6_ci ,
       \n1bit减法_7_ci ;

  \_1bit减法  \u_1bit减法_1  (.A(A0), .B(B0), .Ci(\n1bit减法_1_ci ), .Ci1(Ci_1), .S(S[0]));
  \_1bit减法  \u_1bit减法_2  (.A(A1), .B(B1), .Ci(\n1bit减法_2_ci ), .Ci1(\n1bit减法_1_ci ), .S(S[1]));
  \_1bit减法  \u_1bit减法_3  (.A(A2), .B(B2), .Ci(\n1bit减法_3_ci ), .Ci1(\n1bit减法_2_ci ), .S(S[2]));
  \_1bit减法  \u_1bit减法_4  (.A(A3), .B(B3), .Ci(\n1bit减法_4_ci ), .Ci1(\n1bit减法_3_ci ), .S(S[3]));
  \_1bit减法  \u_1bit减法_5  (.A(A4), .B(B4), .Ci(\n1bit减法_5_ci ), .Ci1(\n1bit减法_4_ci ), .S(S[4]));
  \_1bit减法  \u_1bit减法_6  (.A(A5), .B(B5), .Ci(\n1bit减法_6_ci ), .Ci1(\n1bit减法_5_ci ), .S(S[5]));
  \_1bit减法  \u_1bit减法_7  (.A(A6), .B(B6), .Ci(\n1bit减法_7_ci ), .Ci1(\n1bit减法_6_ci ), .S(S[6]));
  \_1bit减法  \u_1bit减法_8  (.A(A7), .B(B7), .Ci(Ci), .Ci1(\n1bit减法_7_ci ), .S(S[7]));
endmodule

module \_8bit减法最终版  (
  input  Ci_1,
  input  [7:0] A,
  input  [7:0] B,
  output [7:0] S,
  output Ci
);

  \_8bit减法  \u_8bit减法_1  (
    .S(S), .A0(A[0]), .B0(B[0]), .Ci_1(Ci_1), .A1(A[1]), .B1(B[1]), .A2(A[2]), .B2(B[2]), .A3(A[3]),
    .B3(B[3]), .A4(A[4]), .B4(B[4]), .A5(A[5]), .B5(B[5]), .A6(A[6]), .B6(B[6]), .A7(A[7]), .B7(B[7]), .Ci(Ci));
endmodule

module \_32bit减法器  (
  input  Ci_1,
  input  [31:0] A,
  input  [31:0] B,
  output [31:0] S,
  output Ci
);

  wire \n8bit减法最终版_2_ci , \n8bit减法最终版_3_ci , \n8bit减法最终版_4_ci ;

  \_8bit减法最终版  \u_8bit减法最终版_1  (.Ci(Ci), .Ci_1(\n8bit减法最终版_2_ci ), .S(S[31:24]), .A(A[31:24]), .B(B[31:24]));
  \_8bit减法最终版  \u_8bit减法最终版_2  (
    .Ci(\n8bit减法最终版_2_ci ), .Ci_1(\n8bit减法最终版_3_ci ), .S(S[23:16]), .A(A[23:16]), .B(B[23:16]));
  \_8bit减法最终版  \u_8bit减法最终版_3  (
    .Ci(\n8bit减法最终版_3_ci ), .Ci_1(\n8bit减法最终版_4_ci ), .S(S[15:8]), .A(A[15:8]), .B(B[15:8]));
  \_8bit减法最终版  \u_8bit减法最终版_4  (.Ci(\n8bit减法最终版_4_ci ), .Ci_1(Ci_1), .S(S[7:0]), .A(A[7:0]), .B(B[7:0]));
endmodule

module \_32bit加法器最最终版  (
  input  Cin,
  input  [31:0] B,
  input  [31:0] A,
  output [31:0] S,
  output Cout
);

  wire \n8bit加法最终版_2_cout , \n8bit加法最终版_3_cout , \n8bit加法最终版_4_cout ;

  \_8bit加法最终版  \u_8bit加法最终版_1  (.Cout(Cout), .S(S[31:24]), .B(B[31:24]), .A(A[31:24]), .Cin(\n8bit加法最终版_2_cout ));
  \_8bit加法最终版  \u_8bit加法最终版_2  (
    .Cout(\n8bit加法最终版_2_cout ), .S(S[23:16]), .B(B[23:16]), .A(A[23:16]), .Cin(\n8bit加法最终版_4_cout ));
  \_8bit加法最终版  \u_8bit加法最终版_3  (.Cout(\n8bit加法最终版_3_cout ), .S(S[7:0]), .B(B[7:0]), .A(A[7:0]), .Cin(Cin));
  \_8bit加法最终版  \u_8bit加法最终版_4  (
    .Cout(\n8bit加法最终版_4_cout ), .S(S[15:8]), .B(B[15:8]), .A(A[15:8]), .Cin(\n8bit加法最终版_3_cout ));
endmodule

module \补码法减法器  (
  input  [31:0] A,
  input  [31:0] B,
  output [31:0] S
);

  wire [31:0] \n32bit加法器最最终版_1_s , not_1_out;

  assign not_1_out = ~B;  // NOT_Gate not_1, 32 bits wide
  \_32bit加法器最最终版  \u_32bit加法器最最终版_1  (.S(\n32bit加法器最最终版_1_s ), .B(not_1_out), .A(32'h1), .Cin(1'b0));  // open: Cout
  \_32bit加法器最最终版  \u_32bit加法器最最终版_2  (.S(S), .B(A), .A(\n32bit加法器最最终版_1_s ), .Cin(1'b0));  // open: Cout
endmodule
