// Logisim project GPR-v3.circ as structural Verilog: 1 circuit, main circuit main
module main (
  input  [31:0] WD,
  input  [4:0] A1,
  input  [4:0] A2,
  input  WE,
  input  [4:0] A3,
  output [31:0] RD1,
  output [31:0] RD2
);

  wire _01, _02, _03, _04, _05, _06, _07, _08, _09, _10, _11, _12, _13, _14, _15, _16, _17, _18, _19, _20,
       _21, _22, _23, _24, _25, _26, _27, _28, _29, _30, _31, _32, clk_out, reset_out;
  wire [31:0] q01, q02, q03, q04, q05, q06, q07, q08, q09, q10, q11, q12, q13, q14, q15, q16, q17, q18, q19,
       q20, q21, q22, q23, q24, q25, q26, q27, q28, q29, q30, q31, q32;

  Clock clk (.out(clk_out));
  Button reset (.out(reset_out));
  Register #(.width(32)) register_1 (.D(WD), .en(_01), .Q(q01), .clk(clk_out), .clr(reset_out));
  Register #(.width(32)) register_2 (.D(WD), .en(_05), .Q(q05), .clk(clk_out), .clr(reset_out));
  Register #(.width(32)) register_3 (.D(WD), .en(_09), .Q(q09), .clk(clk_out), .clr(reset_out));
  Register #(.width(32)) register_4 (.D(WD), .en(_13), .Q(q13), .clk(clk_out), .clr(reset_out));
  Register #(.width(32)) register_5 (.D(WD), .en(_17), .Q(q17), .clk(clk_out), .clr(reset_out));
  Register #(.width(32)) register_6 (.D(WD), .en(_21), .Q(q21), .clk(clk_out), .clr(reset_out));
  Register #(.width(32)) register_7 (.D(WD), .en(_25), .Q(q25), .clk(clk_out), .clr(reset_out));
  Register #(.width(32)) register_8 (.D(WD), .en(_29), .Q(q29), .clk(clk_out), .clr(reset_out));
  Register #(.width(32)) register_9 (.D(WD), .en(_02), .Q(q02), .clk(clk_out), .clr(reset_out));
  Register #(.width(32)) register_10 (.D(WD), .en(_06), .Q(q06), .clk(clk_out), .clr(reset_out));
  Register #(.width(32)) register_11 (.D(WD), .en(_10), .Q(q10), .clk(clk_out), .clr(reset_out));
  Register #(.width(32)) register_12 (.D(WD), .en(_14), .Q(q14), .clk(clk_out), .clr(reset_out));
  Register #(.width(32)) register_13 (.D(WD), .en(_18), .Q(q18), .clk(clk_out), .clr(reset_out));
  Register #(.width(32)) register_14 (.D(WD), .en(_22), .Q(q22), .clk(clk_out), .clr(reset_out));
  Register #(.width(32)) register_15 (.D(WD), .en(_26), .Q(q26), .clk(clk_out), .clr(reset_out));
  Register #(.width(32)) register_16 (.D(WD), .en(_30), .Q(q30), .clk(clk_out), .clr(reset_out));
  Register #(.width(32)) register_17 (.D(WD), .en(_03), .Q(q03), .clk(clk_out), .clr(reset_out));
  Register #(.width(32)) register_18 (.D(WD), .en(_07), .Q(q07), .clk(clk_out), .clr(reset_out));
  Register #(.width(32)) register_19 (.D(WD), .en(_11), .Q(q11), .clk(clk_out), .clr(reset_out));
  Register #(.width(32)) register_20 (.D(WD), .en(_15), .Q(q15), .clk(clk_out), .clr(reset_out));
  Register #(.width(32)) register_21 (.D(WD), .en(_19), .Q(q19), .clk(clk_out), .clr(reset_out));
  Register #(.width(32)) register_22 (.D(WD), .en(_23), .Q(q23), .clk(clk_out), .clr(reset_out));
  Register #(.width(32)) register_23 (.D(WD), .en(_27), .Q(q27), .clk(clk_out), .clr(reset_out));
  Register #(.width(32)) register_24 (.D(WD), .en(_31), .Q(q31), .clk(clk_out), .clr(reset_out));
  Register #(.width(32)) register_25 (.D(WD), .en(_04), .Q(q04), .clk(clk_out), .clr(reset_out));
  Register #(.width(32)) register_26 (.D(WD), .en(_08), .Q(q08), .clk(clk_out), .clr(reset_out));
  Register #(.width(32)) register_27 (.D(WD), .en(_12), .Q(q12), .clk(clk_out), .clr(reset_out));
  Register #(.width(32)) register_28 (.D(WD), .en(_16), .Q(q16), .clk(clk_out), .clr(reset_out));
  Register #(.width(32)) register_29 (.D(WD), .en(_20), .Q(q20), .clk(clk_out), .clr(reset_out));
  Register #(.width(32)) register_30 (.D(WD), .en(_24), .Q(q24), .clk(clk_out), .clr(reset_out));
  Register #(.width(32)) register_31 (.D(WD), .en(_28), .Q(q28), .clk(clk_out), .clr(reset_out));
  Register #(.width(32)) register_32 (.D(WD), .en(_32), .Q(q32), .clk(clk_out), .clr(reset_out));
  Multiplexer #(.select(5), .width(32)) multiplexer_1 (
    .in0(q01), .in1(q02), .in2(q03), .in3(q04), .in4(q05), .in5(q06), .in6(q07), .in7(q08), .in8(q09),
    .in9(q10), .in10(q11), .in11(q12), .in12(q13), .in13(q14), .in14(q15), .in15(q16), .in16(q17),
    .in17(q18), .in18(q19), .in19(q20), .in20(q21), .in21(q22), .in22(q23), .in23(q24), .in24(q25),
    .in25(q26), .in26(q27), .in27(q28), .in28(q29), .in29(q30), .in30(q31), .in31(q32), .out(RD1), .sel(A1));  // open: en
  Decoder #(.select(5)) decoder_1 (
    .out0(_01), .out1(_02), .out2(_03), .out3(_04), .out4(_05), .out5(_06), .out6(_07), .out7(_08),
    .out8(_09), .out9(_10), .out10(_11), .out11(_12), .out12(_13), .out13(_14), .out14(_15), .out15(_16),
    .out16(_17), .out17(_18), .out18(_19), .out19(_20), .out20(_21), .out21(_22), .out22(_23), .out23(_24),
    .out24(_25), .out25(_26), .out26(_27), .out27(_28), .out28(_29), .out29(_30), .out30(_31), .out31(_32),
    .sel(A3), .en(WE));
  Multiplexer #(.select(5), .width(32)) multiplexer_2 (
    .in0(q01), .in1(q02), .in2(q03), .in3(q04), .in4(q05), .in5(q06), .in6(q07), .in7(q08), .in8(q09),
    .in9(q10), .in10(q11), .in11(q12), .in12(q13), .in13(q14), .in14(q15), .in15(q16), .in16(q17),
    .in17(q18), .in18(q19), .in19(q20), .in20(q21), .in21(q22), .in22(q23), .in23(q24), .in24(q25),
    .in25(q26), .in26(q27), .in27(q28), .in28(q29), .in29(q30), .in30(q31), .in31(q32), .out(RD2), .sel(A2));  // open: en
endmodule
