// Logisim project 八位全加器.circ as structural Verilog: 4 circuits, main circuit 8bit直观版
module \_8bit电路版  (
  input  C0,
  input  A0,
  input  B0,
  input  A1,
  input  B1,
  input  A2,
  input  B2,
  input  A3,
  input  B3,
  input  A4,
  input  B4,
  input  A5,
  input  B5,
  input  A6,
  input  B6,
  input  A7,
  input  B7,
  output S0,
  output S1,
  output S2,
  output S3,
  output S4,
  output S5,
  output S6,
  output S7,
  output C7
);

  wire n4bit_1_c4;

  _4bit u_4bit_1 (
    .C4(n4bit_1_c4), .S3(S3), .S0(S0), .S1(S1), .S2(S2), .A0(A0), .B0(B0), .C0(C0), .A1(A1), .B1(B1),
    .A2(A2), .B2(B2), .A3(A3), .B3(B3));
  _4bit u_4bit_2 (
    .C4(C7), .S3(S7), .S0(S4), .S1(S5), .S2(S6), .A0(A4), .B0(B4), .C0(n4bit_1_c4), .A1(A5), .B1(B5),
    .A2(A6), .B2(B6), .A3(A7), .B3(B7));
endmodule

module _1bit (
  input  A,
  input  B,
  input  Ci,
  output Co,
  output S
);

  wire and_1_out, and_2_out, and_3_out, and_4_out, and_5_out, and_6_out, and_7_out, and_8_out, and_9_out,
       and_10_out, and_11_out, not_1_out, not_2_out, not_3_out, not_4_out, not_5_out, not_6_out, or_1_out,
       or_3_out, or_4_out;

  and and_1 (and_1_out, B, Ci);
  and and_2 (and_2_out, A, Ci);
  not not_1 (not_1_out, B);
  not not_2 (not_2_out, A);
  not not_3 (not_3_out, A);
  not not_4 (not_4_out, B);
  or or_1 (or_1_out, and_1_out, and_2_out);
  and and_3 (and_3_out, A, B);
  and and_4 (and_4_out, A, not_1_out);
  not not_5 (not_5_out, Ci);
  and and_5 (and_5_out, not_2_out, B);
  not not_6 (not_6_out, Ci);
  and and_6 (and_6_out, not_3_out, not_4_out);
  and and_7 (and_7_out, A, B);
  or or_2 (Co, or_1_out, and_3_out);
  and and_8 (and_8_out, and_4_out, not_5_out);
  and and_9 (and_9_out, and_5_out, not_6_out);
  and and_10 (and_10_out, and_6_out, Ci);
  and and_11 (and_11_out, and_7_out, Ci);
  or or_3 (or_3_out, and_8_out, and_9_out);
  or or_4 (or_4_out, and_10_out, and_11_out);
  or or_5 (S, or_3_out, or_4_out);
endmodule

module _4bit (
  input  C0,
  input  A0,
  input  B0,
  input  A1,
  input  B1,
  input  A2,
  input  B2,
  input  A3,
  input  B3,
  output S0,
  output S1,
  output S2,
  output S3,
  output C4
);

  wire n1bit_1_co, n1bit_2_co, n1bit_3_co;

  _1bit u_1bit_1 (.A(A0), .B(B0), .Ci(C0), .Co(n1bit_1_co), .S(S0));
  _1bit u_1bit_2 (.A(A1), .B(B1), .Ci(n1bit_1_co), .Co(n1bit_2_co), .S(S1));
  _1bit u_1bit_3 (.A(A2), .B(B2), .Ci(n1bit_2_co), .Co(n1bit_3_co), .S(S2));
  _1bit u_1bit_4 (.A(A3), .B(B3), .Ci(n1bit_3_co), .Co(C4), .S(S3));
endmodule

module \_8bit直观版  (
  input  Cin,
  input  [7:0] B,
  input  [7:0] A,
  output [7:0] S,
  output Cout
);

  \_8bit电路版  \u_8bit电路版_1  (
    .C0(Cin), .C7(Cout), .S0(S[0]), .S1(S[1]), .S2(S[2]), .S3(S[3]), .S4(S[4]), .S5(S[5]), .S6(S[6]),
    .S7(S[7]), .A0(A[0]), .B0(B[0]), .A1(A[1]), .B1(B[1]), .A2(A[2]), .B2(B[2]), .A3(A[3]), .B3(B[3]),
    .A4(A[4]), .B4(B[4]), .A5(A[5]), .B5(B[5]), .A6(A[6]), .B6(B[6]), .A7(A[7]), .B7(B[7]));
endmodule
